// Logisim project circuit.circ as structural Verilog: 1 circuit, main circuit main
module main (
  input  [3:0] in_1,
  input  [3:0] in_2,
  input  [3:0] in_3,
  input  [3:0] in_4
);

  wire and_1_out, and_2_out, and_3_out, and_4_out, and_5_out, clock_1_out, clock_2_out, comparator_1_eq,
       comparator_2_eq, comparator_3_eq, comparator_4_eq, comparator_5_gt, comparator_6_gt, comparator_7_lt,
       comparator_8_gt, comparator_9_lt, comparator_10_lt, enter_out, lock_out, not_1_out, not_2_out,
       not_3_out, not_4_out, register_1_q, reset_out, start_out;
  wire [2:0] counter_2_q;
  wire [3:0] speed_reg_q, time_counter_q;
  wire [4:0] counter_1_q;

  Button lock (.out(lock_out));
  Button start (.out(start_out));
  Button enter (.out(enter_out));
  Clock #(.highDuration(9)) clock_1 (.out(clock_1_out));
  Clock clock_2 (.out(clock_2_out));
  Comparator #(.width(4)) comparator_1 (.a(4'b0001), .b(in_1), .eq(comparator_1_eq));  // open: gt, lt
  Comparator #(.width(4)) comparator_2 (.a(4'b0010), .b(in_2), .eq(comparator_2_eq));  // open: gt, lt
  Comparator #(.width(4)) comparator_3 (.a(4'b0011), .b(in_3), .eq(comparator_3_eq));  // open: gt, lt
  Comparator #(.width(4)) comparator_4 (.a(4'b0100), .b(in_4), .eq(comparator_4_eq));  // open: gt, lt
  Counter #(.max('h17), .ongoal("load"), .width(5)) counter_1 (
    .up(1'b1), .count(1'b1), .clk(clock_1_out), .Q(counter_1_q));  // open: clr, load, D, carry
  Counter #(.max('hf), .ongoal("stay"), .width(4)) time_counter (
    .clr(start_out), .up(1'b1), .count(1'b1), .clk(clock_2_out), .Q(time_counter_q));  // open: load, D, carry
  Register #(.width(1)) register_1 (.D(and_1_out), .clk(enter_out), .Q(register_1_q), .clr(lock_out));  // open: en
  and and_1 (and_1_out, comparator_1_eq, comparator_2_eq, comparator_3_eq, comparator_4_eq);
  not not_1 (not_1_out, register_1_q);
  Register #(.width(4)) speed_reg (.D(time_counter_q), .clk(enter_out), .Q(speed_reg_q), .clr(start_out));  // open: en
  LED PasswdOK (.in(register_1_q));
  not not_2 (not_2_out, register_1_q);
  and and_2 (and_2_out, not_1_out, enter_out);
  Button reset (.out(reset_out));
  Comparator #(.width(5)) comparator_5 (.a(counter_1_q), .b(5'b11000), .gt(comparator_5_gt));  // open: eq, lt
  Comparator #(.width(5)) comparator_6 (.a(counter_1_q), .b(5'b01000), .gt(comparator_6_gt));  // open: eq, lt
  // Probe on counter_1_q
  Comparator #(.mode("unsigned"), .width(4)) comparator_7 (
    .a(speed_reg_q), .b(4'b0100), .lt(comparator_7_lt));  // open: gt, eq
  Comparator #(.mode("unsigned"), .width(4)) comparator_8 (
    .a(speed_reg_q), .b(4'b1001), .gt(comparator_8_gt));  // open: eq, lt
  Counter #(.max('h7), .ongoal("stay"), .width(3)) counter_2 (
    .clr(reset_out), .up(1'b1), .count(not_2_out), .clk(and_2_out), .Q(counter_2_q));  // open: load, D, carry
  and and_3 (and_3_out, comparator_5_gt, comparator_6_gt);
  not not_3 (not_3_out, comparator_7_lt);
  not not_4 (not_4_out, comparator_8_gt);
  and and_4 (and_4_out, not_3_out, not_4_out);
  // Probe on counter_2_q
  LED time_ok (.in(and_3_out));
  LED speed_ok (.in(and_4_out));
  Comparator #(.mode("unsigned"), .width(3)) comparator_9 (
    .a(counter_2_q), .b(3'b100), .lt(comparator_9_lt));  // open: gt, eq
  Comparator #(.mode("unsigned"), .width(3)) comparator_10 (
    .a(3'b100), .b(counter_2_q), .lt(comparator_10_lt));  // open: gt, eq
  and and_5 (and_5_out, register_1_q, comparator_9_lt, and_4_out, and_3_out);
  LED unlock (.in(and_5_out));
  LED lockout_signal (.in(comparator_10_lt));
endmodule
